# Fritzing sketch YalerCampFire (saved by Fritzing 0.8.3b)
breadboards: 1

parts:
  Arduino_Ethernet_Shield1 = Arduino Ethernet Shield
  red_LED = LED - 5mm [color="Red (633nm)" package="5 mm [THT]"]
  yellow_LED = LED - 5mm [color="Red (633nm)" package="5 mm [THT]"]
  R2_(220_Ohm) = Resistor [tolerance=±5% resistance=220 package=THT]
  R1_(220_Ohm) = Resistor [tolerance=±5% resistance=220 package=THT]

nets (from the schematic view):
  N1: Arduino_Ethernet_Shield1.D6, yellow_LED.cathode
  N2: Arduino_Ethernet_Shield1.D3, red_LED.cathode
  N3: Arduino_Ethernet_Shield1.+5V, R2_(220_Ohm).Pin_0, R1_(220_Ohm).Pin_0
  N4: red_LED.anode, R2_(220_Ohm).Pin_1
  N5: yellow_LED.anode, R1_(220_Ohm).Pin_1
